# Fritzing sketch cyclop (saved by Fritzing 0.7.11b)
perfboards: 18
breadboards: 2

parts:
  Arduino1 = Arduino
  Bauteil1 = Triple Axis Accelerometer Breakout - ADXL335
  RHT1 = Humidity and Temperature Sensor RHT03
  R2 = Resistor [tolerance=±5% resistance=220 package=THT]
  R3 = Photocell (LDR) [package=THT]
  U1 = Arduino Mega
  RHT2 = Humidity and Temperature Sensor RHT03

nets:
  N1: Arduino1.D2, RHT1.Vcc
  N2: Arduino1.+5V, Bauteil1.XOUT, RHT1.GND_1, R2.Pin_0
  GND: Arduino1.GND, Bauteil1.GND, RHT1.GND_2, R3.pin_1
  N3: Arduino1.A5, R3.pin_0
  N4: Arduino1.SCL, Bauteil1.ZOUT
  +5V: U1.+5V, RHT2.Vcc
  N5: U1.GND, RHT2.GND_2
  N6: U1.D24, RHT2.Data-signal

notes:
  RTC ->
  USB Breakout
  Accelerometer
  Temp and Humidity
  Light Sensor
  CO ->
  NO->
  Dust->
  Temp und Hum->
  <-Acceloremer
  <-Button
  Vibration
  LCD->
  RTC->
  <-Water Sensor
  GPS->
  Speaker->
  Microphone->
  SD Breakout
